// Logisim project main8bit.circ as structural Verilog: 16 circuits, main circuit main
module main (
  input  in_1,
  input  in_2,
  input  in_3,
  input  in_4,
  input  in_5,
  input  in_6,
  input  in_7,
  input  in_8,
  input  in_9,
  input  in_10,
  input  in_11,
  input  in_12,
  input  in_13,
  input  in_14,
  input  in_15
);

  wire clock_1_out, not_1_out;
  wire [3:0] cntr_1_cout, controlled_buffer_8_out, MAR_out_8, stpcntr_1_op;
  wire [7:0] alu_1_otpt, Ax_out_14, Bx_out_14, controlled_buffer_1_out, controlled_buffer_2_out,
       controlled_buffer_3_out, controlled_buffer_4_out, InsReg_out_12;
  wire [15:15] rom_1_data;

  Clock clock_1 (.out(clock_1_out));
  Reg8bit Ax (
    .wrten(in_1), .clk(clock_1_out), .in_1(controlled_buffer_1_out[7]), .in_2(controlled_buffer_1_out[6]),
    .in_3(controlled_buffer_1_out[5]), .in_4(controlled_buffer_1_out[4]), .in_5(controlled_buffer_1_out[3]),
    .in_6(controlled_buffer_1_out[2]), .in_7(controlled_buffer_1_out[1]), .in_8(controlled_buffer_1_out[0]),
    .out_15(Ax_out_14[7]), .out_11(Ax_out_14[6]), .out_16(Ax_out_14[5]), .out_12(Ax_out_14[4]),
    .out_17(Ax_out_14[3]), .out_13(Ax_out_14[2]), .out_18(Ax_out_14[1]), .out_14(Ax_out_14[0]));
  Reg8bit Bx (
    .wrten(in_3), .clk(clock_1_out), .in_1(controlled_buffer_2_out[7]), .in_2(controlled_buffer_2_out[6]),
    .in_3(controlled_buffer_2_out[5]), .in_4(controlled_buffer_2_out[4]), .in_5(controlled_buffer_2_out[3]),
    .in_6(controlled_buffer_2_out[2]), .in_7(controlled_buffer_2_out[1]), .in_8(controlled_buffer_2_out[0]),
    .out_15(Bx_out_14[7]), .out_11(Bx_out_14[6]), .out_16(Bx_out_14[5]), .out_12(Bx_out_14[4]),
    .out_17(Bx_out_14[3]), .out_13(Bx_out_14[2]), .out_18(Bx_out_14[1]), .out_14(Bx_out_14[0]));
  Reg8bit InsReg (
    .wrten(in_7), .clk(clock_1_out), .in_1(controlled_buffer_3_out[7]), .in_2(controlled_buffer_3_out[6]),
    .in_3(controlled_buffer_3_out[5]), .in_4(controlled_buffer_3_out[4]), .in_5(controlled_buffer_3_out[3]),
    .in_6(controlled_buffer_3_out[2]), .in_7(controlled_buffer_3_out[1]), .in_8(controlled_buffer_3_out[0]),
    .out_15(InsReg_out_12[7]), .out_11(InsReg_out_12[6]), .out_16(InsReg_out_12[5]),
    .out_12(InsReg_out_12[4]), .out_17(InsReg_out_12[3]), .out_13(InsReg_out_12[2]),
    .out_18(InsReg_out_12[1]), .out_14(InsReg_out_12[0]));
  not not_1 (not_1_out, clock_1_out);
  stpcntr stpcntr_1 (.clk(not_1_out), .OP(stpcntr_1_op));
  assign controlled_buffer_1_out = in_1 ? controlled_buffer_4_out : 8'bz;  // Controlled_Buffer controlled_buffer_1
  assign controlled_buffer_2_out = in_3 ? controlled_buffer_4_out : 8'bz;  // Controlled_Buffer controlled_buffer_2
  ALU alu_1 (.OPslct(in_5), .Ax(Ax_out_14), .Bx(Bx_out_14), .otpt(alu_1_otpt));  // open: aluflg
  assign controlled_buffer_3_out = in_7 ? controlled_buffer_4_out : 8'bz;  // Controlled_Buffer controlled_buffer_3
  assign controlled_buffer_4_out = in_2 ? Ax_out_14 : 8'bz;  // Controlled_Buffer controlled_buffer_4
  assign controlled_buffer_4_out = in_4 ? Bx_out_14 : 8'bz;  // Controlled_Buffer controlled_buffer_5
  assign controlled_buffer_4_out = in_6 ? alu_1_otpt : 8'bz;  // Controlled_Buffer controlled_buffer_6
  assign controlled_buffer_4_out = in_8 ? InsReg_out_12 : 8'bz;  // Controlled_Buffer controlled_buffer_7
  ROM #(.dataWidth(16)) rom_1 (
    .addr({stpcntr_1_op, InsReg_out_12[3:0]}),
    .data({rom_1_data[15], in_1, in_2, in_3, in_4, in_5, in_6, in_7, in_8, in_9, in_10, in_11, in_12, in_13, in_14, in_15}));
  assign controlled_buffer_8_out = in_9 ? controlled_buffer_4_out[3:0] : 4'bz;  // Controlled_Buffer controlled_buffer_8
  RAM #(.addrWidth(4)) ram_1 (
    .addr(MAR_out_8), .we(in_10), .oe(in_11), .clk(clock_1_out), .din(controlled_buffer_4_out),
    .dout(controlled_buffer_4_out));
  bit4reg MAR (
    .in_1(controlled_buffer_8_out[3]), .in_2(controlled_buffer_8_out[2]), .in_3(controlled_buffer_8_out[1]),
    .in_4(controlled_buffer_8_out[0]), .out_9(MAR_out_8[3]), .out_7(MAR_out_8[2]), .out_10(MAR_out_8[1]),
    .out_8(MAR_out_8[0]));  // open: Wrten, clk
  cntr cntr_1 (
    .JUMPsl(in_15), .jmp(controlled_buffer_4_out[3:0]), .clk(clock_1_out), .countEN(in_13), .reset(in_14),
    .cout(cntr_1_cout));
  assign controlled_buffer_4_out[3:0] = in_12 ? cntr_1_cout : 4'bz;  // Controlled_Buffer controlled_buffer_9

  // Notes on the sheet:
  //   contents of rom_1 (hex, n*v repeats v):
  //   120
endmodule

module cntr (
  input  JUMPsl,
  input  [3:0] jmp,
  input  clk,
  input  countEN,
  input  reset,
  output [3:0] cout
);

  wire and_1_out, and_2_out, and_3_out, not_1_out;
  wire [3:0] or4bit_1_out_3;

  or4bit or4bit_1 (.slct(JUMPsl), .bitin(jmp), .out_3(or4bit_1_out_3));
  and and_1 (and_1_out, clk, countEN);
  masterslaveJK masterslavejk_1 (
    .prset(or4bit_1_out_3[0]), .J(1'b1), .K(1'b1), .clk(and_1_out), .clr(not_1_out), .Q(cout[0]));  // open: Qc
  not not_1 (not_1_out, reset);
  and and_2 (and_2_out, cout[0], cout[1]);
  masterslaveJK masterslavejk_2 (
    .prset(or4bit_1_out_3[1]), .J(cout[0]), .K(cout[0]), .clk(and_1_out), .clr(not_1_out), .Q(cout[1]));  // open: Qc
  and and_3 (and_3_out, and_2_out, cout[2]);
  masterslaveJK masterslavejk_3 (
    .prset(or4bit_1_out_3[2]), .J(and_2_out), .K(and_2_out), .clk(and_1_out), .clr(not_1_out), .Q(cout[2]));  // open: Qc
  masterslaveJK masterslavejk_4 (
    .prset(or4bit_1_out_3[3]), .J(and_3_out), .K(and_3_out), .clk(and_1_out), .clr(not_1_out), .Q(cout[3]));  // open: Qc
endmodule

module masterslaveJK (
  input  prset,
  input  J,
  input  K,
  input  clk,
  input  clr,
  output Q,
  output Qc
);

  wire nand_1_out, nand_2_out, nand_3_out, nand_4_out, nand_5_out, nand_6_out, nand_7_out;

  nand nand_1 (nand_1_out, Qc, J, clk);
  nand nand_2 (nand_2_out, clk, K, Q);
  nand nand_3 (nand_3_out, nand_1_out, prset, nand_4_out);
  nand nand_4 (nand_4_out, nand_3_out, clr, nand_2_out);
  nand nand_5 (nand_5_out, clk, clk);
  nand nand_6 (nand_6_out, nand_5_out, nand_3_out);
  nand nand_7 (nand_7_out, nand_4_out, nand_5_out);
  nand nand_8 (Q, nand_6_out, Qc);
  nand nand_9 (Qc, Q, nand_7_out);
endmodule

module or4bit (
  input  slct,
  input  [3:0] bitin,
  output [3:0] out_3
);

  wire and_1_out, and_2_out, and_3_out, and_4_out;
  wire [3:0] or_1_out;

  and and_1 (and_1_out, bitin[0], slct);
  and and_2 (and_2_out, bitin[1], slct);
  and and_3 (and_3_out, bitin[2], slct);
  and and_4 (and_4_out, bitin[3], slct);
  or or_1 (or_1_out[0], and_1_out, 1'b0);
  or or_2 (or_1_out[1], 1'b0, and_2_out);
  or or_3 (or_1_out[2], 1'b0, and_3_out);
  or or_4 (or_1_out[3], 1'b0, and_4_out);
  assign out_3 = ~or_1_out;  // NOT_Gate not_1, 4 bits wide
endmodule

module FlipF (
  input  Din,
  input  WRTen,
  input  clk,
  output Dout
);

  wire nand_1_out, nand_2_out, nand_3_out, nand_5_out;

  nand nand_1 (nand_1_out, Din, Din);
  nand nand_2 (nand_2_out, Din, WRTen, clk);
  nand nand_3 (nand_3_out, clk, WRTen, nand_1_out);
  nand nand_4 (Dout, nand_2_out, nand_5_out);
  nand nand_5 (nand_5_out, Dout, nand_3_out);
endmodule

module bit4reg (
  input  in_1,
  input  in_2,
  input  in_3,
  input  in_4,
  input  Wrten,
  input  clk,
  output out_7,
  output out_8,
  output out_9,
  output out_10
);

  FlipF flipf_1 (.Din(in_1), .WRTen(Wrten), .clk(clk), .Dout(out_9));
  FlipF flipf_2 (.Din(in_2), .WRTen(Wrten), .clk(clk), .Dout(out_7));
  FlipF flipf_3 (.Din(in_3), .WRTen(Wrten), .clk(clk), .Dout(out_10));
  FlipF flipf_4 (.Din(in_4), .WRTen(Wrten), .clk(clk), .Dout(out_8));
endmodule

module Reg8bit (
  input  in_1,
  input  in_2,
  input  in_3,
  input  in_4,
  input  in_5,
  input  in_6,
  input  in_7,
  input  in_8,
  input  wrten,
  input  clk,
  output out_11,
  output out_12,
  output out_13,
  output out_14,
  output out_15,
  output out_16,
  output out_17,
  output out_18
);

  FlipF flipf_1 (.Din(in_1), .WRTen(wrten), .clk(clk), .Dout(out_15));
  FlipF flipf_2 (.Din(in_2), .WRTen(wrten), .clk(clk), .Dout(out_11));
  FlipF flipf_3 (.Din(in_3), .WRTen(wrten), .clk(clk), .Dout(out_16));
  FlipF flipf_4 (.Din(in_4), .WRTen(wrten), .clk(clk), .Dout(out_12));
  FlipF flipf_5 (.Din(in_5), .WRTen(wrten), .clk(clk), .Dout(out_17));
  FlipF flipf_6 (.Din(in_6), .WRTen(wrten), .clk(clk), .Dout(out_13));
  FlipF flipf_7 (.Din(in_7), .WRTen(wrten), .clk(clk), .Dout(out_18));
  FlipF flipf_8 (.Din(in_8), .WRTen(wrten), .clk(clk), .Dout(out_14));
endmodule

module selector (
  input  in_1,
  input  in_2,
  input  [7:0] Iin,
  output [7:0] Io,
  output [7:0] I1
);

  and and_1 (Io[0], Iin[0], in_1);
  and and_2 (Io[1], Iin[1], in_1);
  and and_3 (Io[2], Iin[2], in_1);
  and and_4 (Io[3], Iin[3], in_1);
  and and_5 (Io[4], Iin[4], in_1);
  and and_6 (Io[5], Iin[5], in_1);
  and and_7 (Io[6], Iin[6], in_1);
  and and_8 (Io[7], Iin[7], in_1);
  and and_9 (I1[0], Iin[0], in_2);
  and and_10 (I1[1], Iin[1], in_2);
  and and_11 (I1[2], Iin[2], in_2);
  and and_12 (I1[3], Iin[3], in_2);
  and and_13 (I1[4], Iin[4], in_2);
  and and_14 (I1[5], Iin[5], in_2);
  and and_15 (I1[6], Iin[6], in_2);
  and and_16 (I1[7], Iin[7], in_2);
endmodule

module sub1bit (
  input  Borrow_in,
  input  X,
  input  Y,
  output op,
  output borrow_op
);

  wire nand_1_out, nand_2_out, nand_3_out, nand_4_out, nand_5_out, nand_6_out, nand_7_out;

  nand nand_1 (nand_1_out, X, Y);
  nand nand_2 (nand_2_out, X, nand_1_out);
  nand nand_3 (nand_3_out, nand_1_out, Y);
  nand nand_4 (nand_4_out, nand_2_out, nand_3_out);
  nand nand_5 (nand_5_out, Borrow_in, nand_4_out);
  nand nand_6 (nand_6_out, Borrow_in, nand_5_out);
  nand nand_7 (nand_7_out, nand_5_out, nand_4_out);
  nand nand_8 (op, nand_6_out, nand_7_out);
  nand nand_9 (borrow_op, nand_6_out, nand_3_out);
endmodule

module sub8bit (
  input  Bin,
  input  [7:0] X,
  input  [7:0] Y,
  output [7:0] Diff,
  output Bout
);

  wire sub1bit_1_borrow_op, sub1bit_2_borrow_op, sub1bit_3_borrow_op, sub1bit_4_borrow_op,
       sub1bit_5_borrow_op, sub1bit_6_borrow_op, sub1bit_7_borrow_op;

  sub1bit sub1bit_1 (.Borrow_in(Bin), .X(X[0]), .Y(Y[0]), .op(Diff[0]), .borrow_op(sub1bit_1_borrow_op));
  sub1bit sub1bit_2 (
    .Borrow_in(sub1bit_1_borrow_op), .X(X[1]), .Y(Y[1]), .op(Diff[1]), .borrow_op(sub1bit_2_borrow_op));
  sub1bit sub1bit_3 (
    .Borrow_in(sub1bit_2_borrow_op), .X(X[2]), .Y(Y[2]), .op(Diff[2]), .borrow_op(sub1bit_3_borrow_op));
  sub1bit sub1bit_4 (
    .Borrow_in(sub1bit_3_borrow_op), .X(X[3]), .Y(Y[3]), .op(Diff[3]), .borrow_op(sub1bit_4_borrow_op));
  sub1bit sub1bit_5 (
    .Borrow_in(sub1bit_4_borrow_op), .X(X[4]), .Y(Y[4]), .op(Diff[4]), .borrow_op(sub1bit_5_borrow_op));
  sub1bit sub1bit_6 (
    .Borrow_in(sub1bit_5_borrow_op), .X(X[5]), .Y(Y[5]), .op(Diff[5]), .borrow_op(sub1bit_6_borrow_op));
  sub1bit sub1bit_7 (
    .Borrow_in(sub1bit_6_borrow_op), .X(X[6]), .Y(Y[6]), .op(Diff[6]), .borrow_op(sub1bit_7_borrow_op));
  sub1bit sub1bit_8 (.Borrow_in(sub1bit_7_borrow_op), .X(X[7]), .Y(Y[7]), .op(Diff[7]), .borrow_op(Bout));
endmodule

module singlebitadd (
  input  carry_in,
  input  X,
  input  Y,
  output op,
  output carry_out
);

  wire nand_1_out, nand_2_out, nand_3_out, nand_4_out, nand_5_out, nand_6_out, nand_7_out;

  nand nand_1 (nand_1_out, X, Y);
  nand nand_2 (nand_2_out, X, nand_1_out);
  nand nand_3 (nand_3_out, nand_1_out, Y);
  nand nand_4 (nand_4_out, nand_2_out, nand_3_out);
  nand nand_5 (nand_5_out, carry_in, nand_4_out);
  nand nand_6 (nand_6_out, carry_in, nand_5_out);
  nand nand_7 (nand_7_out, nand_5_out, nand_4_out);
  nand nand_8 (op, nand_6_out, nand_7_out);
  nand nand_9 (carry_out, nand_5_out, nand_1_out);
endmodule

module Adder8bit (
  input  Cin,
  input  [7:0] in_2,
  input  [7:0] in_3,
  output [7:0] Sum,
  output bitovrflw
);

  wire singlebitadd_1_carry_out, singlebitadd_2_carry_out, singlebitadd_3_carry_out,
       singlebitadd_4_carry_out, singlebitadd_5_carry_out, singlebitadd_6_carry_out, singlebitadd_7_carry_out;

  singlebitadd singlebitadd_1 (
    .carry_in(Cin), .X(in_2[0]), .Y(in_3[0]), .op(Sum[0]), .carry_out(singlebitadd_1_carry_out));
  singlebitadd singlebitadd_2 (
    .carry_in(singlebitadd_1_carry_out), .X(in_2[1]), .Y(in_3[1]), .op(Sum[1]),
    .carry_out(singlebitadd_2_carry_out));
  singlebitadd singlebitadd_3 (
    .carry_in(singlebitadd_2_carry_out), .X(in_2[2]), .Y(in_3[2]), .op(Sum[2]),
    .carry_out(singlebitadd_3_carry_out));
  singlebitadd singlebitadd_4 (
    .carry_in(singlebitadd_3_carry_out), .X(in_2[3]), .Y(in_3[3]), .op(Sum[3]),
    .carry_out(singlebitadd_4_carry_out));
  singlebitadd singlebitadd_5 (
    .carry_in(singlebitadd_4_carry_out), .X(in_2[4]), .Y(in_3[4]), .op(Sum[4]),
    .carry_out(singlebitadd_5_carry_out));
  singlebitadd singlebitadd_6 (
    .carry_in(singlebitadd_5_carry_out), .X(in_2[5]), .Y(in_3[5]), .op(Sum[5]),
    .carry_out(singlebitadd_6_carry_out));
  singlebitadd singlebitadd_7 (
    .carry_in(singlebitadd_6_carry_out), .X(in_2[6]), .Y(in_3[6]), .op(Sum[6]),
    .carry_out(singlebitadd_7_carry_out));
  singlebitadd singlebitadd_8 (
    .carry_in(singlebitadd_7_carry_out), .X(in_2[7]), .Y(in_3[7]), .op(Sum[7]), .carry_out(bitovrflw));
endmodule

module ALU (
  input  OPslct,
  input  [7:0] Ax,
  input  [7:0] Bx,
  output [7:0] otpt,
  output aluflg
);

  wire adder8bit_1_bitovrflw, nand_1_out, sub8bit_1_bout;
  wire [7:0] adder8bit_1_sum, selector_1_i1, selector_1_io, selector_2_i1, selector_2_io, sub8bit_1_diff;

  nand nand_1 (nand_1_out, OPslct, OPslct);
  selector selector_1 (.in_1(OPslct), .in_2(nand_1_out), .Iin(Ax), .Io(selector_1_io), .I1(selector_1_i1));
  selector selector_2 (.in_1(OPslct), .in_2(nand_1_out), .Iin(Bx), .Io(selector_2_io), .I1(selector_2_i1));
  sub8bit sub8bit_1 (.X(selector_1_io), .Y(selector_2_io), .Diff(sub8bit_1_diff), .Bout(sub8bit_1_bout));  // open: Bin
  Adder8bit adder8bit_1 (
    .in_2(selector_1_i1), .in_3(selector_2_i1), .Sum(adder8bit_1_sum), .bitovrflw(adder8bit_1_bitovrflw));  // open: Cin
  assign otpt = OPslct ? sub8bit_1_diff : 8'bz;  // Controlled_Buffer controlled_buffer_1
  assign otpt = nand_1_out ? adder8bit_1_sum : 8'bz;  // Controlled_Buffer controlled_buffer_2
  assign aluflg = OPslct ? sub8bit_1_bout : 1'bz;  // Controlled_Buffer controlled_buffer_3
  assign aluflg = nand_1_out ? adder8bit_1_bitovrflw : 1'bz;  // Controlled_Buffer controlled_buffer_4
endmodule

module jkfrstp (
  input  J,
  input  K,
  input  clk,
  output Q,
  output Qc
);

  wire nand_1_out, nand_2_out, nand_3_out, nand_4_out, nand_5_out, nand_6_out, nand_7_out;

  nand nand_1 (nand_1_out, Qc, J, clk);
  nand nand_2 (nand_2_out, clk, K, Q);
  nand nand_3 (nand_3_out, nand_1_out, nand_4_out);
  nand nand_4 (nand_4_out, nand_3_out, nand_2_out);
  nand nand_5 (nand_5_out, clk, clk);
  nand nand_6 (nand_6_out, nand_5_out, nand_3_out);
  nand nand_7 (nand_7_out, nand_4_out, nand_5_out);
  nand nand_8 (Q, nand_6_out, Qc);
  nand nand_9 (Qc, Q, nand_7_out);
endmodule

module stpcntr (
  input  clk,
  output [3:0] OP
);

  wire and_1_out;

  jkfrstp jkfrstp_1 (.J(1'b1), .K(1'b1), .clk(clk), .Q(OP[0]));  // open: Qc
  and and_1 (and_1_out, OP[0], OP[1]);
  jkfrstp jkfrstp_2 (.J(OP[0]), .K(OP[0]), .clk(clk), .Q(OP[1]));  // open: Qc
  jkfrstp jkfrstp_3 (.J(and_1_out), .K(and_1_out), .clk(clk), .Q(OP[2]));  // open: Qc

  assign OP[3] = 1'b0;
endmodule

module decdr (
  input  [2:0] inp,
  output out_2,
  output out_3,
  output out_4,
  output out_5,
  output out_6,
  output out_7,
  output out_8,
  output out_9
);

  wire not_1_out, not_2_out, not_3_out;

  not not_1 (not_1_out, inp[1]);
  not not_2 (not_2_out, inp[1]);
  not not_3 (not_3_out, inp[2]);
  and and_1 (out_2, inp[1], inp[1], inp[2]);
  and and_2 (out_3, inp[1], inp[1], not_3_out);
  and and_3 (out_4, inp[1], not_2_out, inp[2]);
  and and_4 (out_5, inp[1], not_2_out, not_3_out);
  and and_5 (out_6, not_1_out, inp[1], inp[2]);
  and and_6 (out_7, not_1_out, inp[1], inp[2]);
  and and_7 (out_8, not_1_out, inp[1], not_3_out);
  and and_8 (out_9, not_1_out, not_2_out, not_3_out);

  assign inp[0] = inp[1];
endmodule
